# Fritzing sketch ZHSG (saved by Fritzing 0.8.5b)
circuit board: 8.46667cm x 5.64444cm
breadboards: 1

parts:
  Arduino = Arduino Uno (Rev3)
  U1 = Optocoupler [package=THT]
  RE1 = Rotary Encoder [package=THT]  # not connected
  LCD1 = LCD screen  # not connected
  U2 = Voltage Regulator - 5V [package="TO220 [THT]"]
  R2 = Resistor [tolerance=±5% resistance=4.7k package=THT]
  U3 = Optocoupler [package=THT]
  R4 = Resistor [tolerance=±5% resistance=4.7k package=THT]
  LM4040CIZ-5_0-NOPB = TRANSISTOR_NPN [package=to-92]
  R5 = Resistor [tolerance=±5% resistance=540 package=THT]
  R6 = Resistor [tolerance=±5% resistance=22k package=THT]
  R7 = Resistor [tolerance=±5% resistance=47k package=THT]
  R8 = Resistor [tolerance=±5% resistance=22k package=THT]
  R9 = Resistor [tolerance=±5% resistance=47k package=THT]
  R10 = Resistor [tolerance=±5% resistance=4.7k package=THT]
  R11 = Resistor [tolerance=±5% resistance=4.7k package=THT]
  Q1 = MOSFET-NCHANNEL [package=to-92]
  Out = screw terminal, 5 pins
  R12 = Trimmer Potentiometer [maximum_resistance=10kΩ package=THT]
  R13 = Trimmer Potentiometer [maximum_resistance=10kΩ package=THT]
  R14 = Resistor [tolerance=±5% resistance=1k package=THT]
  J1 = longpad pin header, 10 pins [form="long pad"]  # not connected
  IN = screw terminal, 6 pins
  C1 = Electrolytic Capacitor [capacitance=4.7µF package="100 mil [THT, electrolytic]"]
  C2 = Electrolytic Capacitor [capacitance=4.7µF package="100 mil [THT, electrolytic]"]
  L1 = Inductor [inductance=8.7 current=1.5 package="400 mil [THT]"]
  R15 = Resistor [tolerance=±5% resistance=220 package=THT]
  R16 = Resistor [tolerance=±5% resistance=100 package=THT]
  J2 = shrouded pin header, 16 pins [form="♂ (shrouded male)"]

nets:
  N1: Arduino.A0, R6.Pin_1, R7.Pin_0
  N2: Arduino.A1, R8.Pin_1, R9.Pin_0
  N3: Arduino.D11_PWM/MOSI, U1.Pin_5, R2.Pin_1
  N4: Arduino.D12/MISO, U3.Pin_5, R4.Pin_1
  N5: Arduino.D13/SCK, R14.Pin_0
  GND: Arduino.GND, U1.Pin_2, U1.Pin_4, U2.GND, U3.Pin_2, U3.Pin_4, LM4040CIZ-5_0-NOPB.E, R12.wiper, R13.wiper, IN.pin6, C1.-, C2.-, R15.Pin_1, J2.pin1, J2.pin5, J2.pin16
  N6: Arduino.AREF, LM4040CIZ-5_0-NOPB.B, R5.Pin_1
  5V: Arduino.5V, U2.output_voltage, R2.Pin_0, R4.Pin_0, R5.Pin_0, J2.pin2
  N7: U1.Pin_1, R10.Pin_1
  N8: U2.input_voltage, C2.+, L1.pin_1
  N9: U3.Pin_1, R11.Pin_1
  12V: R6.Pin_0, IN.pin2
  N10: R7.Pin_1, R12.leg2
  N11: R8.Pin_0, IN.pin1, C1.+, L1.pin_0
  N12: R9.Pin_1, R13.leg2
  N13: R10.Pin_0, IN.pin3
  N14: R11.Pin_0, IN.pin4
  N15: Q1.S, Out.pin1
  N16: Q1.G, R14.Pin_1
  N17: IN.pin5, R16.Pin_1
  N18: R15.Pin_0, R16.Pin_0, J2.pin15

notes:
  Spannungsmessung Batt. 1
  Spannungsmessung Batt. 2
  12 V Zweitbatterie
  GND
  Zündung
  Zuheizer
  12 V Hauptbatterie
  Trennrelais
  Zuheizer Steuergerät
  Amaturenbel
  4,5V / 45mA
  Spannungsreferenz
